// Logisim project alu.circ as structural Verilog: 1 circuit, main circuit ALU
module ALU (
  input  [31:0] A,
  input  [31:0] B,
  input  [3:0] ALU_Op,
  output [31:0] Out
);

  wire comparator_1_lt;
  wire [31:0] _0_sll, _1_srl, _2_add, _3_and, _4_or, _5_xor, _6_slt, _7_mul, _8_mulh, _9_div, _10_rem,
       _11_sub;

  Adder #(.width(32)) adder_1 (.a(A), .b(B), .out(_2_add));  // open: cin, cout
  Shifter #(.width(32)) shifter_1 (.in(A), .\dist (B[4:0]), .out(_0_sll));
  Shifter #(.width(32), .shift("lr")) shifter_2 (.in(A), .\dist (B[4:0]), .out(_1_srl));
  assign _3_and = A & B;  // AND_Gate and_1, 32 bits wide
  assign _4_or = A | B;  // OR_Gate or_1, 32 bits wide
  assign _5_xor = A ^ B;  // XOR_Gate xor_1, 32 bits wide
  Comparator #(.width(32)) comparator_1 (.a(A), .b(B), .lt(comparator_1_lt));  // open: gt, eq
  Multiplier #(.width(32)) multiplier_1 (.a(A), .b(B), .out(_7_mul), .cout(_8_mulh));  // open: cin
  Divider #(.width(32)) divider_1 (.a(A), .b(B), .out(_9_div), .rem(_10_rem));  // open: upper
  Subtractor #(.width(32)) subtractor_1 (.a(A), .b(B), .out(_11_sub));  // open: bin, bout
  assign _6_slt = {{31{1'b0}}, comparator_1_lt};  // Bit_Extender bit_extender_1
  Multiplexer #(.select(4), .width(32)) multiplexer_1 (
    .in0(_0_sll), .in1(_1_srl), .in2(_2_add), .in3(_3_and), .in4(_4_or), .in5(_5_xor), .in6(_6_slt),
    .in7(_7_mul), .in8(_8_mulh), .in9(_9_div), .in10(_10_rem), .in11(_11_sub), .in12({32{1'b1}}),
    .in13({32{1'b1}}), .in14({32{1'b1}}), .in15({32{1'b1}}), .out(Out), .sel(ALU_Op));  // open: en

  // Other names for the same wires on the sheet: Op[3:0] = ALU_Op

  // Notes on the sheet:
  //   Inputs
  //   NOTE
  //   Please do not modify/replace/move/change/delete/etc input and output pins
  //   Outputs
endmodule
