// Logisim project cpu.circ as structural Verilog: 5 circuits, main circuit CPU
module CPU (
  input  [31:0] Instruction,
  input  CLK,
  output [31:0] s0,
  output [31:0] s1,
  output [31:0] t0,
  output [31:0] t1,
  output [31:0] a0,
  output [31:0] ra,
  output [31:0] sp,
  output [31:0] PC
);

  wire Asel, BrEq, BrLT, BrUn, Bsel, MemRW, PCSel, RegWEn;
  wire [1:0] WBSel;
  wire [2:0] ImmSel;
  wire [3:0] ALUSel;
  wire [4:0] rdIMEM, rs1IMEM, rs2IMEM;
  wire [31:0] A, ALU_out, B, ImmGen_out, INSTIMEM, multiplexer_1_out, pc_4, pc_t, plus_4, R1, R2, Read_Data,
       wb;

  // Incrementer incrementer_1: pin names not known; wires that end beside it: plus_4
  Multiplexer #(.width(32)) multiplexer_1 (
    .in0(ALU_out), .in1(pc_4), .out(multiplexer_1_out), .sel(PCSel));  // open: en
  Register #(.width(32)) register_1 (.D(pc_4), .Q(PC), .clk(CLK));  // open: en, clr
  // PC pc_1: pin names not known; wires that end beside it: multiplexer_1_out, CLK, pc_t
  Adder #(.width(32)) adder_1 (.a(pc_t), .b(plus_4), .out(pc_4));  // open: cin, cout
  IMEM imem_1 (.Entrada_PC(pc_t), .inst_11_7(rdIMEM), .inst_19_15(rs1IMEM), .inst_24_20(rs2IMEM), .ins_31_0(INSTIMEM));
  ImmGen immgen_1 (.Instruction(INSTIMEM), .in_2(ImmSel), .Immediate(ImmGen_out));
  RegFile regfile_1 (
    .Clk(CLK), .R1(R1), .R2(R2), .WE(RegWEn), .W(wb), .RD(rdIMEM), .RS1(rs1IMEM), .RS2(rs2IMEM), .s0(s0),
    .s1(s1), .t0(t0), .t1(t1), .a0(a0), .ra(ra), .sp(sp));
  Branch_Comp branch_comp_1 (.R1(R1), .R2(R2), .in_3(BrUn), .BrEq(BrEq), .BrLT(BrLT));
  Multiplexer #(.width(32)) multiplexer_2 (.in0(R1), .in1(pc_t), .out(A), .sel(Asel));  // open: en
  Multiplexer #(.width(32)) multiplexer_3 (.in0(R2), .in1(ImmGen_out), .out(B), .sel(Bsel));  // open: en
  ControlUnit controlunit_1 (
    .Inst_30(Instruction[30]), .Inst_14_12(Instruction[14:12]), .Inst_6_2(Instruction[6:2]), .BrEq(BrLT),
    .BrLT(BrEq), .PCSel(PCSel), .ImmSel(ImmSel), .BrUn(BrUn), .Asel(Asel), .Bsel(Bsel), .ALUSel(ALUSel),
    .MemRW(MemRW), .RegWEn(RegWEn), .WBSel(WBSel));
  ALU alu_1 (.A(A), .B(B), .ALU_Op(ALUSel), .Out(ALU_out));
  // memory_main main_1: pin names not known; wires that end beside it: ALU_out, MemRW, R2, CLK, Read_Data
  Multiplexer #(.select(2), .width(32)) multiplexer_4 (
    .in0(Read_Data), .in1(ALU_out), .in2(pc_4), .out(wb), .sel(WBSel));  // open: in3, en

  // Other names for the same wires on the sheet: _6_2[4:0] = Instruction[6:2]; INST[31:0] = Instruction;
  //   opcode[6:0] = Instruction[6:0]; _14_12[2:0] = Instruction[14:12]; funct3[2:0] = Instruction[14:12];
  //   fetch_addr[31:0] = PC; funct7[6:0] = Instruction[31:25]; _30 = Instruction[30]; rd[4:0] = Instruction[11:7];
  //   rs1[4:0] = Instruction[19:15]; rs2[4:0] = Instruction[24:20]

  // Notes on the sheet:
  //   NOTE
  //   Please do not modify/replace/move/change/delete/etc input and output pins
  //   These are debug/test outputs from your circuit
endmodule

module ImmGen (
  input  [31:0] Instruction,
  input  [2:0] in_2,
  output [31:0] Immediate
);

  wire [31:0] tipo_B, tipo_I, tipo_S;

  assign tipo_I = {{20{Instruction[31]}}, Instruction[31:20]};  // Bit_Extender bit_extender_1
  assign tipo_S = {{20{Instruction[31]}}, {Instruction[31:25], Instruction[11:7]}};  // Bit_Extender bit_extender_2
  assign tipo_B = {{20{Instruction[7]}}, {Instruction[7], Instruction[30:25], Instruction[11:8], 1'b0}};  // Bit_Extender bit_extender_3
  Multiplexer #(.select(3), .width(32)) multiplexer_1 (
    .in0(tipo_I), .in1(tipo_S), .in2(tipo_B), .in3({Instruction[31:12], {12{1'b0}}}),
    .in4({{12{1'b0}}, Instruction[31], Instruction[19:13], Instruction[20], Instruction[30:21], 1'b0}),
    .in5({32{1'b0}}), .in6({32{1'b0}}), .in7({32{1'b0}}), .out(Immediate), .sel(in_2));  // open: en

  // Other names for the same wires on the sheet: instruc[31:0] = Instruction; Immedate[31:0] = Immediate;
  //   ImmSel[2:0] = in_2; tipo_J[19:1] = {Instruction[31], Instruction[19:13], Instruction[20], Instruction[30:21]};
  //   tipo_U[31:12] = Instruction[31:12]

  // Notes on the sheet:
  //   Inputs
  //   TIPO I
  //   TIPO S
  //   TIPO B
  //   Extras:
  //   Output:
  //   TIPO U
  //   TIPO J
endmodule

module ControlUnit (
  input  Inst_30,
  input  [2:0] Inst_14_12,
  input  [4:0] Inst_6_2,
  input  BrEq,
  input  BrLT,
  output PCSel,
  output [2:0] ImmSel,
  output BrUn,
  output Asel,
  output Bsel,
  output [3:0] ALUSel,
  output MemRW,
  output RegWEn,
  output [1:0] WBSel
);

  ROM #(.addrWidth(11), .dataWidth(15)) rom_1 (
    .addr({Inst_30, Inst_14_12, Inst_6_2, BrEq, BrLT}),
    .data({WBSel, RegWEn, MemRW, ALUSel, Bsel, Asel, BrUn, ImmSel, PCSel}), .sel(1'b1));

  // Notes on the sheet:
  //   Inputs
  //   contents of rom_1 (hex, n*v repeats v):
  //   20 820 1020 1820 2020 2820 3020 3820 4020 4820 5020 5820 30 1830 2030 3030 3830 1030 2830 31 31 31
  //   250 a04 1a04 1e14 68 104c 4c
  //   Outputs
endmodule

module Branch_Comp (
  input  [31:0] R1,
  input  [31:0] R2,
  input  in_3,
  output BrEq,
  output BrLT
);

  wire Con, Sin;

  Comparator #(.width(32)) comparator_1 (.a(R1), .b(R2), .eq(BrEq));  // open: gt, lt
  Comparator #(.width(32)) comparator_2 (.a(R1), .b(R2), .lt(Con));  // open: gt, eq
  Comparator #(.width(32), .mode("unsigned")) comparator_3 (.a(R1), .b(R2), .lt(Sin));  // open: gt, eq
  Multiplexer multiplexer_1 (.in0(Con), .in1(Sin), .out(BrLT), .sel(in_3));  // open: en

  // Other names for the same wires on the sheet: BrUn = in_3

  // Notes on the sheet:
  //   Inputs:
  //   Outputs:
endmodule

module IMEM (
  input  [31:0] Entrada_PC,
  output [4:0] inst_11_7,
  output [4:0] inst_19_15,
  output [4:0] inst_24_20,
  output [31:0] ins_31_0
);

  ROM #(.addrWidth(5), .dataWidth(32)) rom_1 (.addr(Entrada_PC[6:2]), .data(ins_31_0));  // open: sel

  assign inst_11_7 = ins_31_0[11:7];
  assign inst_19_15 = ins_31_0[19:15];
  assign inst_24_20 = ins_31_0[24:20];

  // Other names for the same wires on the sheet: EntradaPC[31:0] = Entrada_PC
endmodule
