// Logisim project regfile.circ as structural Verilog: 2 circuits, main circuit RegFile
module RegFile (
  input  [4:0] RD,
  input  [4:0] RS1,
  input  [4:0] RS2,
  input  [31:0] W,
  input  WE,
  input  Clk,
  output [31:0] s0,
  output [31:0] s1,
  output [31:0] t0,
  output [31:0] t1,
  output [31:0] a0,
  output [31:0] ra,
  output [31:0] sp,
  output [31:0] R1,
  output [31:0] R2
);

  wire and_1_out, and_2_out, and_3_out, and_4_out, and_5_out, and_6_out, and_7_out, and_8_out, x0, x1, x2,
       x5, x6, x8, x9, x10, x11;
  wire [31:0] a1, zero;

  Decoder_part #(.select(5)) decoder_1 (
    .out0(x0), .out1(x1), .out2(x2), .out5(x5), .out6(x6), .out8(x8), .out9(x9), .out10(x10), .out11(x11),
    .sel(RD));  // open: out3, out4, out7, out12, out13, out14, out15, out16, out17, out18, out19, out20, out21, out22, out23, out24, out25, out26, out27, out28, out29, out30, out31, en
  and and_1 (and_1_out, x1, WE);
  and and_2 (and_2_out, x2, WE);
  and and_3 (and_3_out, x5, WE);
  and and_4 (and_4_out, x6, WE);
  and and_5 (and_5_out, x8, WE);
  and and_6 (and_6_out, x9, WE);
  and and_7 (and_7_out, x10, WE);
  and and_8 (and_8_out, x11, WE);
  Register #(.width(32)) x0_zero (.en(1'b0), .Q(zero), .clk(Clk));  // open: D, clr
  Register #(.width(32)) x1_ra (.D(W), .en(and_1_out), .Q(ra), .clk(Clk));  // open: clr
  Register #(.width(32)) x2_sp (.D(W), .en(and_2_out), .Q(sp), .clk(Clk));  // open: clr
  Register #(.width(32)) x5_t0 (.D(W), .en(and_3_out), .Q(t0), .clk(Clk));  // open: clr
  Register #(.width(32)) x6_t1 (.D(W), .en(and_4_out), .Q(t1), .clk(Clk));  // open: clr
  Register #(.width(32)) x8_s0 (.D(W), .en(and_5_out), .Q(s0), .clk(Clk));  // open: clr
  Register #(.width(32)) x9_s1 (.D(W), .en(and_6_out), .Q(s1), .clk(Clk));  // open: clr
  Register #(.width(32)) x10_a0 (.D(W), .en(and_7_out), .Q(a0), .clk(Clk));  // open: clr
  Register #(.width(32)) x11_a1 (.D(W), .en(and_8_out), .Q(a1), .clk(Clk));  // open: clr
  Multiplexer #(.select(5), .width(32)) multiplexer_1 (
    .in0(zero), .in1(ra), .in2(sp), .in3({32{1'b1}}), .in4({32{1'b1}}), .in5(t0), .in6(t1), .in7({32{1'b1}}),
    .in8(s0), .in9(s1), .in10(a0), .in11(a1), .in12({32{1'b1}}), .in13({32{1'b1}}), .in14({32{1'b1}}),
    .in15({32{1'b1}}), .in16({32{1'b1}}), .in17({32{1'b1}}), .in18({32{1'b1}}), .in19({32{1'b1}}),
    .in20({32{1'b1}}), .in21({32{1'b1}}), .in22({32{1'b1}}), .in23({32{1'b1}}), .in24({32{1'b1}}),
    .in25({32{1'b1}}), .in26({32{1'b1}}), .in27({32{1'b1}}), .in28({32{1'b1}}), .in29({32{1'b1}}),
    .in30({32{1'b1}}), .in31({32{1'b1}}), .out(R1), .sel(RS1));  // open: en
  Multiplexer #(.select(5), .width(32)) multiplexer_2 (
    .in0(zero), .in1(ra), .in2(sp), .in3({32{1'b1}}), .in4({32{1'b1}}), .in5(t0), .in6(t1), .in7({32{1'b1}}),
    .in8(s0), .in9(s1), .in10(a0), .in11(a1), .in12({32{1'b1}}), .in13({32{1'b1}}), .in14({32{1'b1}}),
    .in15({32{1'b1}}), .in16({32{1'b1}}), .in17({32{1'b1}}), .in18({32{1'b1}}), .in19({32{1'b1}}),
    .in20({32{1'b1}}), .in21({32{1'b1}}), .in22({32{1'b1}}), .in23({32{1'b1}}), .in24({32{1'b1}}),
    .in25({32{1'b1}}), .in26({32{1'b1}}), .in27({32{1'b1}}), .in28({32{1'b1}}), .in29({32{1'b1}}),
    .in30({32{1'b1}}), .in31({32{1'b1}}), .out(R2), .sel(RS2));  // open: en

  // Notes on the sheet:
  //   Write Register
  //   Read Register 1
  //   Read Register 2
  //   Write Data
  //   Write Enable
  //   Clock
  //   NOTE
  //   Please do not modify/replace/move/change/delete/etc input and output pins
  //   These are debug/test outputs from your circuit
  //   Read Data 1
  //   Read Data 2
endmodule

module Decoder (
  input  [31:0] Instruccion
);


  assign {Instruccion[30:25], Instruccion[23:20], Instruccion[18:15], Instruccion[13:12], Instruccion[10:7], Instruccion[5:0]} = {{6{Instruccion[31]}}, {4{Instruccion[24]}}, {4{Instruccion[19]}}, {2{Instruccion[14]}}, {4{Instruccion[11]}}, {6{Instruccion[6]}}};

  // Other names for the same wires on the sheet: Opcode = Instruccion[6]; rd = Instruccion[11];
  //   funct3 = Instruccion[14]; rs1 = Instruccion[19]; rs2 = Instruccion[24]; funct7 = Instruccion[31]
endmodule
